# Fritzing sketch DistanceSensor Sketch (saved by Fritzing 0.9.3b)
breadboards: 1

parts:
  Part1 = SRF05 Ultrasonic Rangefinder
  Part2 = Adafruit Metro M0 Express

nets:
  VCC: Part1.VCC, Part2.+5V
  N1: Part1.Trig, Part2.D6
  N2: Part1.Echo, Part2.D7
  GND: Part1.GND, Part2.GND

custom parts:
  Adafruit Metro M0 Express: Metro is our series of microcontroller boards for use with the Arduino IDE. This new Metro board looks a whole lot like our original Metro 328, but with a huge upgrade. Instead of the ATmega328, this Metro features a ATSAMD21G18 chip, an ARM Cortex M0+. It's our first Metro that is designed for use with CircuitPython! CircuitPython is our beginner-oriented flavor of MicroPython - and as the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
