# Fritzing sketch famcyLED Sketch (saved by Fritzing 0.9.3b)
breadboards: 1

parts:
  R1 = Resistor [tolerance=±5% resistance=220 package=THT]
  R2 = Resistor [tolerance=±5% resistance=220 package=THT]
  R3 = Resistor [tolerance=±5% resistance=220 package=THT]
  R4 = Resistor [tolerance=±5% resistance=220 package=THT]
  R5 = Resistor [tolerance=±5% resistance=220 package=THT]
  R6 = Resistor [tolerance=±5% resistance=220 package=THT]
  Part1 = Adafruit Metro M0 Express
  LED2 = LED - 5mm [color="Red (633nm)" package="5 mm [THT]"]
  LED3 = LED - 5mm [color="Red (633nm)" package="5 mm [THT]"]
  LED4 = LED - 5mm [color="Red (633nm)" package="5 mm [THT]"]
  LED5 = LED - 5mm [color="Red (633nm)" package="5 mm [THT]"]
  LED6 = LED - 5mm [color="Red (633nm)" package="5 mm [THT]"]
  LED7 = LED - 5mm [color="Red (633nm)" package="5 mm [THT]"]

nets:
  N1: R1.Pin_0, LED3.cathode
  N2: R1.Pin_1, Part1.D7
  N3: R2.Pin_0, LED2.cathode
  N4: R2.Pin_1, Part1.D6
  N5: R3.Pin_0, LED7.cathode
  N6: R3.Pin_1, Part1.D5
  N7: R4.Pin_0, LED6.cathode
  N8: R4.Pin_1, Part1.D4
  N9: R5.Pin_0, LED5.cathode
  N10: R5.Pin_1, Part1.D3
  N11: R6.Pin_0, LED4.cathode
  N12: R6.Pin_1, Part1.D2
  N13: Part1.GND, LED2.anode, LED3.anode, LED4.anode, LED5.anode, LED6.anode, LED7.anode

custom parts:
  Adafruit Metro M0 Express: Metro is our series of microcontroller boards for use with the Arduino IDE. This new Metro board looks a whole lot like our original Metro 328, but with a huge upgrade. Instead of the ATmega328, this Metro features a ATSAMD21G18 chip, an ARM Cortex M0+. It's our first Metro that is designed for use with CircuitPython! CircuitPython is our beginner-oriented flavor of MicroPython - and as the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
